# Fritzing sketch Roduinoscope (saved by Fritzing 0.9.3b)
perfboards: 1

parts:
  J1 = male pin header, 6 pins [form="♂ (male)"]
  J2 = male pin header, 6 pins [form="♂ (male)"]
  J3 = male pin header, 8 pins [form="♂ (male)"]  # not connected
  J4 = male pin header, 11 pins [form="♂ (male)"]
  J5 = female pin header, 8 pins [form="♀ (female)" part_number="TFT Screen"]
  S2 = Momentary Switch [package=ksa_sealed_tac_switch]
  R1 = Resistor [tolerance=±5% resistance=1k package="0805 [SMD]"]
  J6 = female pin header, 2 pins [form="♀ (female)"]
  J7 = female pin header, 1 pin [form="♀ (female)"]

nets:
  N1: J1.pin1, J5.pin4
  N2: J1.pin2, J5.pin5
  N3: J1.pin4, J5.pin6
  N4: J1.pin6, J5.pin7
  N5: J2.pin1, J6.pin1
  N6: J4.pin7, J6.pin2
  N7: J4.pin8, J5.pin8
  N8: S2.2, R1.Pin_0
  N9: S2.4, J7.pin1
